# Fritzing sketch diagrama (saved by Fritzing 1.0.4)
breadboards: 1

parts:
  Mod1 = Amica NodeMCU DEVKIT 1.0
  M1 = RioRand LM2596
  VCC1 = 4 x AAA Battery Mount [internal_resistance=0.1Ω]  # not connected
  VCC2 = 4 x AAA Battery Mount [internal_resistance=0.1Ω]  # not connected
  M6 = gear-motor
  M7 = gear-motor
  M8 = gear-motor
  M9 = gear-motor
  S1 = H-Bridge with L298N
  S2 = H-Bridge with L298N
  HC-SR04_Sensor_1 = HC-SR04 Ultrasonic Distance Sensor
  TCRT1 = TCRT5000 digital module [part_number=151608]
  S3 = Pushbutton [package=THT]
  TCRT2 = TCRT5000 digital module [part_number=151608]
  TCRT3 = TCRT5000 digital module [part_number=151608]
  TCRT4 = TCRT5000 digital module [part_number=151608]

nets:
  N1: Mod1.pin1, Mod1.pin_10, Mod1.pin_26
  GND: Mod1.pin2, Mod1.pin_9, Mod1.pin_25, Mod1.pin_29, M1.Pin_4, S1.GND, S2.GND, HC-SR04_Sensor_1.GND, TCRT1.GND, TCRT2.GND, TCRT3.GND, TCRT4.GND
  VCC: Mod1.pin_30, S2.5V, HC-SR04_Sensor_1.VCC, TCRT1.VCC, TCRT2.VCC, TCRT3.VCC, TCRT4.VCC
  N2: M1.Pin_1, S3.leg1
  12V: M1.Pin_3, S1.12V, S2.12V
  N3: M6.pin_1, S2.M2-01
  N4: M6.pin_2, S2.M2-02
  N5: M7.pin_1, S1.M1-02
  N6: M7.pin_2, S1.M1-01
  N7: M8.pin_1, S2.M1-02
  N8: M8.pin_2, S2.M1-01
  N9: M9.pin_1, S1.M2-01
  N10: M9.pin_2, S1.M2-02

notes:
  Cada suporte possui 6V, os dois são ligados em série para somar 12V (Foram utilizados 12V para maior duração da alimentação).
  O conversor deve ser regulado em 7.5V, sua saída liga as duas pontes H.
  Uma L298N fica responsável pela alimentação de 5V dos sensores e ESP32.
  5V
  Botão Liga/Desliga
  A ligação das pontes H e dos sensores no ESP32 depende exclusivamente de quais pinos serão utilizados, por esse motivo não realizei a ligação neste diagrama.
  O uso de um protoboard facilita o momento da montagem do robô, evitando diversos Jumpers na alimentação elétrica.
  A ideia de utilizar duas L298N vem da necessidade de movimentar os quatro motores com movimentos unicos entre si, porém é possível utilizar uma unica L298N, tudo depende de sua necessidade.

custom parts:
  H-Bridge with L298N: h-bridge
  TCRT5000 digital module: breakout board for TCRT5000 module, convert analog to digital - Uses TCRT5000 infrared reflectance sensor - Detection distance: 1mm~8mm - Focus distance: 2.5mm - Working voltage: 3.3V~12V - Uses wide voltage LM393 comparator - With multi-turn precision potentiometer to adjust the sensitivity - Current: > 15mA - Output type: Digital switch output (0, 1) - Suitable for watt-hour meter pulse data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
